// Logisim project Cache.circ as structural Verilog
module Cache_Line (
  input  In_Valid,
  input  [13:0] In_Tag,
  input  [31:0] In_W0,
  input  [31:0] In_W1,
  input  [31:0] In_W2,
  input  [31:0] In_W3,
  input  Clk,
  input  Write_En,
  output out_9,
  output [13:0] out_10,
  output [31:0] out_11,
  output [31:0] out_12,
  output [31:0] out_13,
  output [31:0] out_14
);

  Register #(.width(1)) Valid (.D(In_Valid), .Q(out_9));  // open: en, clk, clr
  Register #(.width(14)) Tag (.D(In_Tag), .Q(out_10));  // open: en, clk, clr
  Register #(.width(32)) Word0 (.D(In_W0), .Q(out_11), .clk(Clk), .clr(Write_En));  // open: en
  Register #(.width(32)) Word1 (.D(In_W1), .Q(out_12), .clk(Clk), .clr(Write_En));  // open: en
  Register #(.width(32)) Word2 (.D(In_W2), .Q(out_13), .clk(Clk), .clr(Write_En));  // open: en
  Register #(.width(32)) Word3 (.D(In_W3), .Q(out_14), .clk(Clk), .clr(Write_En));  // open: en
endmodule

module Cache_System (
  input  [31:0] Address,
  input  Cache_Write,
  input  Clk,
  input  [31:0] RAM_O0,
  input  [31:0] RAM_O1,
  input  [31:0] RAM_O2,
  input  [31:0] RAM_O3,
  output [31:0] CPU_ReadData,
  output [13:0] Tag_Leido,
  output Hit,
  output Bit_V_Leido
);

  wire cache_line_1_out_9, cache_line_2_out_9, cache_line_3_out_9, cache_line_4_out_9, comparator_1_eq,
       decoder_1_out0, decoder_1_out1, decoder_1_out2, decoder_1_out3, Write_En_0, Write_En_1, Write_En_2,
       Write_En_3;
  wire [13:0] cache_line_1_out_10, cache_line_2_out_10, cache_line_3_out_10, cache_line_4_out_10;
  wire [31:0] multiplexer_3_out, multiplexer_4_out, multiplexer_5_out, multiplexer_6_out, Out_W0_0, Out_W0_1,
       Out_W0_2, Out_W0_3, Out_W1_0, Out_W1_1, Out_W1_2, Out_W1_3, Out_W2_0, Out_W2_1, Out_W2_2, Out_W2_3,
       Out_W3_0, Out_W3_1, Out_W3_2, Out_W3_3;

  Cache_Line cache_line_1 (
    .In_Valid(1'b1), .In_Tag(Address[19:6]), .Clk(Clk), .Write_En(Write_En_0), .out_9(cache_line_1_out_9),
    .out_10(cache_line_1_out_10), .out_11(Out_W0_0), .out_12(Out_W1_0), .out_13(Out_W2_0), .out_14(Out_W3_0),
    .In_W0(RAM_O0), .In_W1(RAM_O1), .In_W2(RAM_O2), .In_W3(RAM_O3));
  Cache_Line cache_line_2 (
    .In_Valid(1'b1), .In_Tag(Address[19:6]), .Clk(Clk), .Write_En(Write_En_1), .out_9(cache_line_2_out_9),
    .out_10(cache_line_2_out_10), .out_11(Out_W0_1), .out_12(Out_W1_1), .out_13(Out_W2_1), .out_14(Out_W3_1),
    .In_W0(RAM_O0), .In_W1(RAM_O1), .In_W2(RAM_O2), .In_W3(RAM_O3));
  Cache_Line cache_line_3 (
    .In_Valid(1'b1), .In_Tag(Address[19:6]), .Clk(Clk), .Write_En(Write_En_2), .out_9(cache_line_3_out_9),
    .out_10(cache_line_3_out_10), .out_11(Out_W0_2), .out_12(Out_W1_2), .out_13(Out_W2_2), .out_14(Out_W3_2),
    .In_W0(RAM_O0), .In_W1(RAM_O1), .In_W2(RAM_O2), .In_W3(RAM_O3));
  Cache_Line cache_line_4 (
    .In_Valid(1'b1), .In_Tag(Address[19:6]), .Clk(Clk), .Write_En(Write_En_3), .out_9(cache_line_4_out_9),
    .out_10(cache_line_4_out_10), .out_11(Out_W0_3), .out_12(Out_W1_3), .out_13(Out_W2_3), .out_14(Out_W3_3),
    .In_W0(RAM_O0), .In_W1(RAM_O1), .In_W2(RAM_O2), .In_W3(RAM_O3));
  Decoder #(.select(2)) decoder_1 (
    .out0(decoder_1_out0), .out1(decoder_1_out1), .out2(decoder_1_out2), .out3(decoder_1_out3),
    .sel(Address[5:4]));  // open: en
  Multiplexer #(.select(2), .width(14)) multiplexer_1 (
    .in0(cache_line_1_out_10), .in1(cache_line_2_out_10), .in2(cache_line_3_out_10),
    .in3(cache_line_4_out_10), .out(Tag_Leido), .sel(Address[5:4]));  // open: en
  Multiplexer #(.select(2)) multiplexer_2 (
    .in0(cache_line_1_out_9), .in1(cache_line_2_out_9), .in2(cache_line_3_out_9), .in3(cache_line_4_out_9),
    .out(Bit_V_Leido), .sel(Address[5:4]));  // open: en
  Comparator #(.width(14)) comparator_1 (.a(Address[19:6]), .b(Tag_Leido), .eq(comparator_1_eq));  // open: gt, lt
  and and_1 (Write_En_0, decoder_1_out0, Cache_Write);
  and and_2 (Write_En_1, decoder_1_out1, Cache_Write);
  and and_3 (Write_En_2, decoder_1_out2, Cache_Write);
  and and_4 (Write_En_3, decoder_1_out3, Cache_Write);
  and and_5 (Hit, comparator_1_eq, Bit_V_Leido);
  Multiplexer #(.select(2), .width(32)) multiplexer_3 (
    .in0(Out_W0_0), .in1(Out_W0_1), .in2(Out_W0_2), .in3(Out_W0_3), .out(multiplexer_3_out),
    .sel(Address[5:4]));  // open: en
  Multiplexer #(.select(2), .width(32)) multiplexer_4 (
    .in0(Out_W1_0), .in1(Out_W1_1), .in2(Out_W1_2), .in3(Out_W1_3), .out(multiplexer_4_out),
    .sel(Address[5:4]));  // open: en
  Multiplexer #(.select(2), .width(32)) multiplexer_5 (
    .in0(Out_W2_0), .in1(Out_W2_1), .in2(Out_W2_2), .in3(Out_W2_3), .out(multiplexer_5_out),
    .sel(Address[5:4]));  // open: en
  Multiplexer #(.select(2), .width(32)) multiplexer_6 (
    .in0(Out_W3_0), .in1(Out_W3_1), .in2(Out_W3_2), .in3(Out_W3_3), .out(multiplexer_6_out),
    .sel(Address[5:4]));  // open: en
  Multiplexer #(.select(2), .width(32)) multiplexer_7 (
    .in0(multiplexer_3_out), .in1(multiplexer_4_out), .in2(multiplexer_5_out), .in3(multiplexer_6_out),
    .out(CPU_ReadData), .sel(Address[3:2]));  // open: en

  // Other names for the same wires on the sheet: Word_Sel[1:0] = Address[3:2]; Index[1:0] = Address[5:4];
  //   Tag[13:0] = Address[19:6]
endmodule

module Cache_Controller (
  input  Clk,
  input  Reset,
  input  Hit,
  input  MemRead,
  input  MemWrite,
  output Stall,
  output Cache_Write,
  output Ram_CS,
  output Ram_RW
);

  wire [0:0] and_1_out, Current_State;
  wire [1:0] multiplexer_1_out;

  Register #(.width(2)) u_Current_State (
    .D(multiplexer_1_out), .en(Reset), .Q({Cache_Write, Current_State[0]}), .clk(Clk));  // open: clr
  and and_1 (and_1_out[0], ~Hit, MemRead);  // AND_Gate
  or or_1 (Stall, Current_State[0], Cache_Write);
  Multiplexer #(.select(2), .width(2)) multiplexer_1 (
    .in0({1'b0, and_1_out[0]}), .in1(2'b10), .in2(2'b00), .in3(2'b00), .out(multiplexer_1_out),
    .sel({Cache_Write, Current_State[0]}));  // open: en
  or or_2 (Ram_CS, Current_State[0], MemWrite);

  assign Ram_RW = MemWrite;

  // Other names for the same wires on the sheet: Current_State[1] = Cache_Write
endmodule
