// Logisim project ALU.circ as structural Verilog: 5 circuits, main circuit ALU
module ALU (
  input  [31:0] Data_A,
  input  [31:0] Data_B,
  input  [3:0] Selector,
  output [31:0] ALU_Low,
  output Zero,
  output Negative,
  output [31:0] ALU_High
);

  wire slt_bit, sltu_bit;
  wire [31:0] Add, And, DivHigh, DivLow, DivuHigh, DivuLow, MultHigh, MultLow, MuluHigh, MuluLow, Nor, Or,
       slt, sltu, Sub, Xor;

  // Probe on Selector
  Adder #(.width(32)) adder_1 (.a(Data_A), .b(Data_B), .out(Add));  // open: cin, cout
  Multiplier #(.width(32)) multiplier_1 (.a(Data_A), .b(Data_B), .out(MuluLow), .cout(MuluHigh));  // open: cin
  Subtractor #(.width(32)) subtractor_1 (.a(Data_A), .b(Data_B), .out(Sub));  // open: bin, bout
  Divider #(.width(32)) divider_1 (.a(Data_A), .b(Data_B), .out(DivuLow), .rem(DivuHigh));  // open: upper
  // Probe on Data_A
  // Probe on Data_B
  Comparator #(.width(32)) comparator_1 (.a(Data_A), .b(Data_B), .lt(slt_bit));  // open: gt, eq
  assign slt = {{31{1'b0}}, slt_bit};  // Bit_Extender bit_extender_1
  SignedMult signedmult_1 (.in_1(Data_A), .in_2(Data_B), .MultLow(MultLow), .MultHigh(MultHigh));
  SignedDiv signeddiv_1 (.in_1(Data_A), .in_2(Data_B), .MultLow(DivLow), .MultHigh(DivHigh));
  Comparator #(.width(32), .mode("unsigned")) comparator_2 (.a(Data_A), .b(Data_B), .gt(sltu_bit));  // open: eq, lt
  assign sltu = {{31{1'b0}}, sltu_bit};  // Bit_Extender bit_extender_2
  Multiplexer #(.select(4), .width(32), .enable("false")) multiplexer_1 (
    .in0(Add), .in1(Sub), .in2(slt), .in3(sltu), .in4(And), .in5(Or), .in6(Nor), .in7(Xor), .in8(MultLow),
    .in9(MuluLow), .in10(DivLow), .in11(DivuLow), .out(ALU_Low), .sel(Selector));  // open: in12, in13, in14, in15
  Multiplexer #(.select(2), .width(32), .enable("false")) multiplexer_2 (
    .in0(MultHigh), .in1(MuluHigh), .in2(DivHigh), .in3(DivuHigh), .out(ALU_High), .sel(Selector[1:0]));
  // Probe on ALU_Low
  // Probe on ALU_High
  assign And = Data_A & Data_B;  // AND_Gate and_1, 32 bits wide
  assign Or = Data_A | Data_B;  // OR_Gate or_1, 32 bits wide
  assign Nor = ~(Data_A | Data_B);  // NOR_Gate nor_1, 32 bits wide
  assign Xor = Data_A ^ Data_B;  // XOR_Gate xor_1, 32 bits wide
  Comparator #(.width(32)) comparator_3 (.a(ALU_Low), .b({32{1'b0}}), .eq(Zero), .lt(Negative));  // open: gt

  // Other names for the same wires on the sheet: A[31:0] = Data_A; B[31:0] = Data_B;
  //   SelectorHigh[1:0] = Selector[1:0]
endmodule

module SignedMult (
  input  [31:0] in_1,
  input  [31:0] in_2,
  output [31:0] MultLow,
  output [31:0] MultHigh
);

  wire neg_1_out_4, SignResult;
  wire [31:0] absA, absB, multiplier_1_cout, multiplier_1_out, neg_1_out_3, neg_2_out_3;

  xor xor_1 (SignResult, in_1[31], in_2[31]);
  Abs abs_1 (.Data_A(in_1), .Abs_A(absA), .Selector(in_1[31]));
  Abs abs_2 (.Data_A(in_2), .Abs_A(absB), .Selector(in_2[31]));
  Multiplier #(.width(32)) multiplier_1 (
    .a(absA), .b(absB), .out(multiplier_1_out), .cout(multiplier_1_cout));  // open: cin
  Neg neg_1 (.Data_A(multiplier_1_out), .out_3(neg_1_out_3), .out_4(neg_1_out_4));  // open: in_1
  Neg neg_2 (.Data_A(multiplier_1_cout), .out_3(neg_2_out_3), .in_1(neg_1_out_4));  // open: out_4
  Multiplexer #(.width(32)) multiplexer_1 (
    .in0(multiplier_1_out), .in1(neg_1_out_3), .out(MultLow), .sel(SignResult));  // open: en
  Multiplexer #(.width(32)) multiplexer_2 (
    .in0(multiplier_1_cout), .in1(neg_2_out_3), .out(MultHigh), .sel(SignResult));  // open: en
  // Probe on MultLow
  // Probe on MultHigh

  // Other names for the same wires on the sheet: A[31:0] = in_1; SignA = in_1[31]; B[31:0] = in_2; SignB = in_2[31]
endmodule

module Abs (
  input  [31:0] Data_A,
  input  Selector,
  output [31:0] Abs_A
);

  wire [31:0] adder_1_out, not_1_out;

  assign not_1_out = ~Data_A;  // NOT_Gate not_1, 32 bits wide
  Adder #(.width(32)) adder_1 (.a(not_1_out), .b(32'h1), .out(adder_1_out));  // open: cin, cout
  Multiplexer #(.width(32)) multiplexer_1 (.in0(Data_A), .in1(adder_1_out), .out(Abs_A), .sel(Selector));  // open: en

  // Other names for the same wires on the sheet: A[31:0] = Data_A
endmodule

module Neg (
  input  in_1,
  input  [31:0] Data_A,
  output [31:0] out_3,
  output out_4
);

  wire [31:0] not_1_out;

  assign not_1_out = ~Data_A;  // NOT_Gate not_1, 32 bits wide
  Adder #(.width(32)) adder_1 (.a(not_1_out), .b(32'h1), .out(out_3), .cin(in_1), .cout(out_4));

  // Other names for the same wires on the sheet: A[31:0] = Data_A
endmodule

module SignedDiv (
  input  [31:0] in_1,
  input  [31:0] in_2,
  output [31:0] MultLow,
  output [31:0] MultHigh
);

  wire neg_1_out_4, SignResult;
  wire [31:0] absA, absB, divider_1_out, divider_1_rem, neg_1_out_3, neg_2_out_3;

  xor xor_1 (SignResult, in_1[31], in_2[31]);
  Abs abs_1 (.Data_A(in_1), .Abs_A(absA), .Selector(in_1[31]));
  Abs abs_2 (.Data_A(in_2), .Abs_A(absB), .Selector(in_2[31]));
  Divider #(.width(32)) divider_1 (.a(absA), .b(absB), .out(divider_1_out), .rem(divider_1_rem));  // open: upper
  Neg neg_1 (.Data_A(divider_1_out), .out_3(neg_1_out_3), .out_4(neg_1_out_4));  // open: in_1
  Neg neg_2 (.Data_A(divider_1_rem), .out_3(neg_2_out_3), .in_1(neg_1_out_4));  // open: out_4
  Multiplexer #(.width(32)) multiplexer_1 (
    .in0(divider_1_out), .in1(neg_1_out_3), .out(MultLow), .sel(SignResult));  // open: en
  Multiplexer #(.width(32)) multiplexer_2 (
    .in0(divider_1_rem), .in1(neg_2_out_3), .out(MultHigh), .sel(SignResult));  // open: en
  // Probe on MultLow
  // Probe on MultHigh

  // Other names for the same wires on the sheet: A[31:0] = in_1; SignA = in_1[31]; B[31:0] = in_2; SignB = in_2[31]
endmodule
