// Logisim project DataPath.circ as structural Verilog: 2 circuits, main circuit main
module main (
  input  in_1,
  input  in_2,
  input  in_3,
  input  [1:0] in_4,
  input  [1:0] in_5,
  input  in_6,
  input  in_7,
  input  in_8,
  input  in_9,
  input  in_10,
  input  [3:0] in_11,
  input  in_12,
  input  in_13
);

  wire alu_1_zero_flag, and_1_out, or_1_out;
  wire [4:0] multiplexer_2_out;
  wire [27:0] Instr_q, shifter_2_out;
  wire [31:0] A_q, alu_1_result, ALUOut_q, B_q, bit_extender_1_out, Data_q, instruction_memory_1_out_4,
       main_2_a, main_2_b, multiplexer_1_out, multiplexer_3_out, multiplexer_4_out, multiplexer_5_out,
       multiplexer_6_out, PC, shifter_1_out;
  wire [31:28] Instr_q_2;

  PC_main main_1 (.Input(multiplexer_6_out), .Enable(or_1_out), .Clk(in_1), .Output(PC));  // open: Reset
  Multiplexer #(.width(32)) multiplexer_1 (.in0(PC), .in1(ALUOut_q), .out(multiplexer_1_out), .sel(in_3));  // open: en
  Instruction_Memory instruction_memory_1 (
    .in_2(multiplexer_1_out), .in_1(in_1), .in_3(B_q), .out_4(instruction_memory_1_out_4));
  Register #(.width(32)) Instr (
    .D(instruction_memory_1_out_4), .en(in_6), .Q({Instr_q_2, Instr_q}), .clk(in_1));  // open: clr
  Register #(.width(32)) Data (.D(instruction_memory_1_out_4), .Q(Data_q), .clk(in_1));  // open: en, clr
  Multiplexer #(.width(5)) multiplexer_2 (
    .in0(Instr_q[20:16]), .in1(Instr_q[15:11]), .out(multiplexer_2_out), .sel(in_10));  // open: en
  Multiplexer #(.width(32)) multiplexer_3 (
    .in0(ALUOut_q), .in1(Data_q), .out(multiplexer_3_out), .sel(in_12));  // open: en
  Register_File_main main_2 (
    .Data_Input(multiplexer_3_out), .R_W(in_13), .clock(in_1), .Data_Address(multiplexer_2_out),
    .Selector_A(Instr_q[25:21]), .Selector_B(Instr_q[20:16]), .A(main_2_a), .B(main_2_b));  // open: reset, SOp, PC_enable, High_in, Low_in, Hi_Lo_enable, Stack_Pointer, High_Out, Low_Out
  assign bit_extender_1_out = {{16{Instr_q[15]}}, Instr_q[15:0]};  // Bit_Extender bit_extender_1
  Register #(.width(32)) A (.D(main_2_a), .Q(A_q), .clk(in_1));  // open: en, clr
  Register #(.width(32)) B (.D(main_2_b), .Q(B_q), .clk(in_1));  // open: en, clr
  Shifter #(.width(32)) shifter_1 (.in(bit_extender_1_out), .\dist (5'b00010), .out(shifter_1_out));
  Multiplexer #(.width(32)) multiplexer_4 (.in0(PC), .in1(A_q), .out(multiplexer_4_out), .sel(in_2));  // open: en
  Multiplexer #(.select(2), .width(32)) multiplexer_5 (
    .in0(B_q), .in1(32'h4), .in2(bit_extender_1_out), .in3(shifter_1_out), .out(multiplexer_5_out), .sel(in_4));  // open: en
  Shifter #(.width(28)) shifter_2 (.in(Instr_q), .\dist (5'b00010), .out(shifter_2_out));
  ALU alu_1 (
    .in_1(multiplexer_4_out), .in_2(multiplexer_5_out), .in_3(in_11), .Result(alu_1_result),
    .Zero_Flag(alu_1_zero_flag));  // open: Equal, Helper_Result, Sign
  and and_1 (and_1_out, in_7, alu_1_zero_flag);
  Register #(.width(32)) ALUOut (.D(alu_1_result), .Q(ALUOut_q), .clk(in_1));  // open: en, clr
  or or_1 (or_1_out, in_9, and_1_out);
  Multiplexer #(.select(2), .width(32)) multiplexer_6 (
    .in0(alu_1_result), .in1(ALUOut_q), .in2({PC[31:28], shifter_2_out}), .out(multiplexer_6_out), .sel(in_5));  // open: in3, en

  // Other names for the same wires on the sheet: ALUControl[3:0] = in_11; ALUSrcA = in_2; ALUSrcB[1:0] = in_4;
  //   Branch = in_7; Clk = in_1; IorD = in_3; IRWrite = in_6; MemtoReg = in_12; MemWrite = in_8; PCSrc[1:0] = in_5;
  //   PCWrite = in_9; R_W = in_13; RegDst = in_10

  // Notes on the sheet:
  //   ALU+4
endmodule

module Instruction_Memory (
  input  in_1,
  input  [31:0] in_2,
  input  [31:0] in_3,
  output [31:0] out_4
);
endmodule
